// Logisim project ARITMÉTICA 10 BITS.circ as structural Verilog: 1 circuit, main circuit main
// ARITMÉTICA
module main (
  input  B_3,
  input  A_3,
  input  B_2,
  input  A_2,
  input  B_3_2,
  input  A_3_2,
  input  B_2_2,
  input  A_2_2,
  input  B_1,
  input  A_1,
  input  B_0,
  input  A_0,
  input  B_3_3,
  input  A_3_3,
  input  B_2_3,
  input  A_2_3,
  input  B_1_2,
  input  A_1_2,
  input  B_0_2,
  input  A_0_2,
  input  Cin,
  input  S_0,
  input  S_1,
  output Cout,
  output C_3,
  output Q_3,
  output Q_2,
  output Q_3_2,
  output Q_2_2,
  output Q_0,
  output Q_0_2,
  output Q_3_3,
  output Q_2_3,
  output Q_1,
  output Q_1_2
);

  wire _1_out, main_2_cout, main_4_cout, main_5_cout, main_6_cout, main_7_cout, main_8_cout, main_9_cout,
       main_10_cout, main_11_y;

  SST_main main_1 (.A(A_3), .B(B_3), .Q(Q_3), .Cin(C_3), .Cout(Cout), .S(S_0));
  SST_main main_2 (.A(A_3_2), .B(B_3_2), .Q(Q_3_2), .Cin(main_4_cout), .Cout(main_2_cout), .S(S_0));
  SST_main main_3 (.A(A_2), .B(B_2), .Q(Q_2), .Cin(main_2_cout), .Cout(C_3), .S(S_0));
  SST_main main_4 (.A(A_2_2), .B(B_2_2), .Q(Q_2_2), .Cin(main_5_cout), .Cout(main_4_cout), .S(S_0));
  SST_main main_5 (.A(A_1), .B(B_1), .Q(Q_0), .Cin(main_6_cout), .Cout(main_5_cout), .S(S_0));
  SST_main main_6 (.A(A_0), .B(B_0), .Q(Q_0_2), .Cin(main_7_cout), .Cout(main_6_cout), .S(S_0));
  SST_main main_7 (.A(A_3_3), .B(B_3_3), .Q(Q_3_3), .Cin(main_8_cout), .Cout(main_7_cout), .S(S_0));
  SST_main main_8 (.A(A_2_3), .B(B_2_3), .Q(Q_2_3), .Cin(main_9_cout), .Cout(main_8_cout), .S(S_0));
  SST_main main_9 (.A(A_1_2), .B(B_1_2), .Q(Q_1), .Cin(main_10_cout), .Cout(main_9_cout), .S(S_0));
  SST_main main_10 (.A(A_0_2), .B(B_0_2), .Q(Q_1_2), .Cin(main_11_y), .Cout(main_10_cout), .S(S_0));
  not _1 (_1_out, Cin);
  MUX_3_X_1_main main_11 (.E_1(S_0), .E_2(Cin), .E_3(_1_out), .S_1(S_0), .S_0(S_1), .Y(main_11_y));
endmodule
