// Logisim project BIT A BIT 10 BITS.circ as structural Verilog: 1 circuit, main circuit main
// BIT A BIT 10 BIT TR
module main (
  input  A_0,
  input  A_1,
  input  A_2,
  input  A_3,
  input  A_4,
  input  A_5,
  input  A_6,
  input  A_7,
  input  A_8,
  input  A_9,
  input  B_0,
  input  B_1,
  input  B_2,
  input  B_3,
  input  B_4,
  input  B_5,
  input  B_6,
  input  B_7,
  input  B_8,
  input  B_9,
  output NAND_0,
  output NAND_1,
  output NAND_2,
  output NAND_3,
  output NAND_4,
  output NAND_5,
  output NAND_6,
  output NAND_7,
  output NAND_8,
  output NAND_9,
  output NOR_0,
  output NOR_1,
  output NOR_2,
  output NOR_3,
  output NOR_4,
  output NOR_5,
  output NOR_6,
  output NOR_7,
  output NOR_8,
  output NOR_9,
  output XOR_0,
  output XOR_1,
  output XOR_2,
  output XOR_3,
  output XOR_4,
  output XOR_5,
  output XOR_6,
  output XOR_7,
  output XOR_8,
  output XOR_9
);

  // BIT_A_BIT_main main_1: pin names not known; wires that end beside it: A_0, B_0, NAND_0, NOR_0, XOR_0
  // BIT_A_BIT_main main_2: pin names not known; wires that end beside it: A_1, B_1, NAND_1, NOR_1, XOR_1
  // BIT_A_BIT_main main_3: pin names not known; wires that end beside it: A_2, B_2, NAND_2, NOR_2, XOR_2
  // BIT_A_BIT_main main_4: pin names not known; wires that end beside it: A_3, B_3, NAND_3, NOR_3, XOR_3
  // BIT_A_BIT_main main_5: pin names not known; wires that end beside it: A_4, B_4, NAND_4, NOR_4, XOR_4
  // BIT_A_BIT_main main_6: pin names not known; wires that end beside it: A_5, B_5, NAND_5, NOR_5, XOR_5
  // BIT_A_BIT_main main_7: pin names not known; wires that end beside it: A_6, B_6, NAND_6, NOR_6, XOR_6
  // BIT_A_BIT_main main_8: pin names not known; wires that end beside it: A_7, B_7, NAND_7, NOR_7, XOR_7
  // BIT_A_BIT_main main_9: pin names not known; wires that end beside it: A_8, B_8, NAND_8, NOR_8, XOR_8
  // BIT_A_BIT_main main_10: pin names not known; wires that end beside it: A_9, B_9, NAND_9, NOR_9, XOR_9
endmodule
