// Logisim project COMPARADOR 10 BITS.circ as structural Verilog: 1 circuit, main circuit main
// COMPARADOR
module main (
  input  Cout,
  input  C_2,
  input  Q_0,
  input  Q_1,
  input  Q_2,
  input  Q_3,
  input  Q_4,
  input  Q_5,
  input  Q_6,
  input  Q_7,
  input  Q_8,
  input  Q_9,
  input  B_9,
  input  B_8,
  input  B_7,
  input  B_6,
  input  B_5,
  input  B_4,
  input  B_3,
  input  B_2,
  input  B_1,
  input  B_0,
  input  A_9,
  input  A_8,
  input  A_7,
  input  A_6,
  input  A_5,
  input  A_4,
  input  A_3,
  input  A_2,
  input  A_1,
  input  A_0,
  output OVER_FLOW,
  output A___B,
  output A___0,
  output A___B_2,
  output B___0,
  output A___B_3
);

  wire _4_out, _5_out, _6_out, _8_out, _11_out, _12_out, _13_out;

  nor _3 (B___0, B_9, B_8, B_7, B_6, B_5, B_4, B_3, B_2, B_1, B_0);
  nor _2 (A___0, A_9, A_8, A_7, A_6, A_5, A_4, A_3, A_2, A_1, A_0);
  nor _1 (A___B, Q_0, Q_1, Q_2, Q_3, Q_4, Q_5, Q_6, Q_7, Q_8, Q_9);
  not _11 (_11_out, A___B);
  xnor _8 (_8_out, A_9, B_9);
  not _12 (_12_out, A_9);
  and _4 (_4_out, Cout, _11_out, _8_out);
  and _5 (_5_out, _11_out, _12_out, B_9);
  and _6 (_6_out, _11_out, _12_out, B___0);
  not _13 (_13_out, A___B_2);
  and _7 (A___B_3, _13_out, _11_out);
  xor _9 (OVER_FLOW, C_2, Cout);
  or _10 (A___B_2, _4_out, _5_out, _6_out);
endmodule
