// Logisim project DESLOCAMENTO 10 BITS.circ as structural Verilog: 1 circuit, main circuit main
// DESLOCAMENTO
module main (
  input  D_9,
  input  D_8,
  input  D_7,
  input  D_6,
  input  D_5,
  input  D_4,
  input  D_3,
  input  D_2,
  input  D_1,
  input  D_0,
  input  S_0,
  input  S1,
  output Y_9,
  output Y_8,
  output Y_7,
  output Y_6,
  output Y_5,
  output Y_4,
  output Y_3,
  output Y_2,
  output Y_1,
  output Y_0
);

  wire main_1_p5, main_1_p6, main_1_p7, main_1_p8, main_2_dy_anterior, main_2_not_s1_2, main_2_s1_2,
       main_3_dy_anterior, \main_3_dy_próximo , main_3_not_s1_2, main_3_s1_2, main_4_dy_anterior,
       \main_4_dy_próximo , main_4_not_s1_2, main_4_s1_2, main_5_dy_anterior, \main_5_dy_próximo ,
       main_5_not_s1_2, main_5_s1_2, main_6_dy_anterior, \main_6_dy_próximo , main_6_not_s1_2, main_6_s1_2,
       main_7_dy_anterior, \main_7_dy_próximo , main_7_not_s1_2, main_7_s1_2, main_8_dy_anterior,
       \main_8_dy_próximo , main_8_not_s1_2, main_8_s1_2, main_9_dy_anterior, \main_9_dy_próximo ,
       main_9_not_s1_2, \main_10_dy_próximo ;

  // FIM_main main_1: pin names not known; wires that end beside it: S_0, S1, D_9, Y_9, main_1_p5, main_1_p6, main_1_p7, main_1_p8
  MEIO_main main_2 (
    .S1(main_1_p5), .NOT_S1(main_1_p6), .\DY_PRÓXIMO (main_1_p7), .\YD_PRÓXIMO (main_1_p8), .D(D_8), .Y(Y_8),
    .S1_2(main_2_s1_2), .NOT_S1_2(main_2_not_s1_2), .YD_ANTERIOR(\main_3_dy_próximo ),
    .DY_ANTERIOR(main_2_dy_anterior));
  MEIO_main main_3 (
    .S1(main_2_s1_2), .NOT_S1(main_2_not_s1_2), .\DY_PRÓXIMO (\main_3_dy_próximo ),
    .\YD_PRÓXIMO (main_2_dy_anterior), .D(D_7), .Y(Y_7), .S1_2(main_3_s1_2), .NOT_S1_2(main_3_not_s1_2),
    .YD_ANTERIOR(\main_4_dy_próximo ), .DY_ANTERIOR(main_3_dy_anterior));
  MEIO_main main_4 (
    .S1(main_3_s1_2), .NOT_S1(main_3_not_s1_2), .\DY_PRÓXIMO (\main_4_dy_próximo ),
    .\YD_PRÓXIMO (main_3_dy_anterior), .D(D_6), .Y(Y_6), .S1_2(main_4_s1_2), .NOT_S1_2(main_4_not_s1_2),
    .YD_ANTERIOR(\main_5_dy_próximo ), .DY_ANTERIOR(main_4_dy_anterior));
  MEIO_main main_5 (
    .S1(main_4_s1_2), .NOT_S1(main_4_not_s1_2), .\DY_PRÓXIMO (\main_5_dy_próximo ),
    .\YD_PRÓXIMO (main_4_dy_anterior), .D(D_5), .Y(Y_5), .S1_2(main_5_s1_2), .NOT_S1_2(main_5_not_s1_2),
    .YD_ANTERIOR(\main_6_dy_próximo ), .DY_ANTERIOR(main_5_dy_anterior));
  MEIO_main main_6 (
    .S1(main_5_s1_2), .NOT_S1(main_5_not_s1_2), .\DY_PRÓXIMO (\main_6_dy_próximo ),
    .\YD_PRÓXIMO (main_5_dy_anterior), .D(D_4), .Y(Y_4), .S1_2(main_6_s1_2), .NOT_S1_2(main_6_not_s1_2),
    .YD_ANTERIOR(\main_7_dy_próximo ), .DY_ANTERIOR(main_6_dy_anterior));
  MEIO_main main_7 (
    .S1(main_6_s1_2), .NOT_S1(main_6_not_s1_2), .\DY_PRÓXIMO (\main_7_dy_próximo ),
    .\YD_PRÓXIMO (main_6_dy_anterior), .D(D_3), .Y(Y_3), .S1_2(main_7_s1_2), .NOT_S1_2(main_7_not_s1_2),
    .YD_ANTERIOR(\main_8_dy_próximo ), .DY_ANTERIOR(main_7_dy_anterior));
  MEIO_main main_8 (
    .S1(main_7_s1_2), .NOT_S1(main_7_not_s1_2), .\DY_PRÓXIMO (\main_8_dy_próximo ),
    .\YD_PRÓXIMO (main_7_dy_anterior), .D(D_2), .Y(Y_2), .S1_2(main_8_s1_2), .NOT_S1_2(main_8_not_s1_2),
    .YD_ANTERIOR(\main_9_dy_próximo ), .DY_ANTERIOR(main_8_dy_anterior));
  MEIO_main main_9 (
    .S1(main_8_s1_2), .NOT_S1(main_8_not_s1_2), .\DY_PRÓXIMO (\main_9_dy_próximo ),
    .\YD_PRÓXIMO (main_8_dy_anterior), .D(D_1), .Y(Y_1), .NOT_S1_2(main_9_not_s1_2),
    .YD_ANTERIOR(\main_10_dy_próximo ), .DY_ANTERIOR(main_9_dy_anterior));  // open: S1_2
  \INÍCIO_main  main_10 (
    .NOT_S1(main_9_not_s1_2), .\DY_PRÓXIMO (\main_10_dy_próximo ), .\YD_PRÓXIMO (main_9_dy_anterior),
    .D_0(D_0), .Q_0(Y_0));
endmodule
