// Logisim project INÍCIO.circ as structural Verilog: 1 circuit, main circuit main
// INÍC
module main (
  input  D_0,
  input  NOT_S1,
  input  \YD_PRÓXIMO ,
  output \DY_PRÓXIMO ,
  output Q_0
);

  and _7 (\DY_PRÓXIMO , NOT_S1, D_0);

  assign Q_0 = \YD_PRÓXIMO ;
endmodule
