// Logisim project MEIO.circ as structural Verilog: 1 circuit, main circuit main
// MEIO
module main (
  input  D,
  input  S1,
  input  NOT_S1,
  input  YD_ANTERIOR,
  input  \YD_PRÓXIMO ,
  output S1_2,
  output NOT_S1_2,
  output \DY_PRÓXIMO ,
  output DY_ANTERIOR,
  output Y
);

  and _3 (\DY_PRÓXIMO , NOT_S1, D);
  and _4 (DY_ANTERIOR, D, S1);
  or _9 (Y, \YD_PRÓXIMO , YD_ANTERIOR);

  assign NOT_S1_2 = NOT_S1;
  assign S1_2 = S1;
endmodule
