// Logisim project MUX 2 X 1 10 BITS.circ as structural Verilog: 1 circuit, main circuit main
// MUX 2 X 1 10 BITS
module main (
  input  B9,
  input  B8,
  input  B7,
  input  B6,
  input  B5,
  input  B4,
  input  B3,
  input  B2,
  input  B1,
  input  B0,
  input  A9,
  input  A8,
  input  A7,
  input  A6,
  input  A5,
  input  A4,
  input  A3,
  input  A2,
  input  A1,
  input  A0,
  input  S,
  output Y9,
  output Y8,
  output Y7,
  output Y6,
  output Y5,
  output Y4,
  output Y3,
  output Y2,
  output Y1,
  output Y0
);

  MUX_2_X_1_main main_1 (.E_1(A9), .E_2(B9), .S(S), .Y(Y9));
  MUX_2_X_1_main main_2 (.E_1(A7), .E_2(B7), .S(S), .Y(Y7));
  MUX_2_X_1_main main_3 (.E_1(A8), .E_2(B8), .S(S), .Y(Y8));
  MUX_2_X_1_main main_4 (.E_1(A6), .E_2(B6), .S(S), .Y(Y6));
  MUX_2_X_1_main main_5 (.E_1(A5), .E_2(B5), .S(S), .Y(Y5));
  MUX_2_X_1_main main_6 (.E_1(A4), .E_2(B4), .S(S), .Y(Y4));
  MUX_2_X_1_main main_7 (.E_1(A3), .E_2(B3), .S(S), .Y(Y3));
  MUX_2_X_1_main main_8 (.E_1(A2), .E_2(B2), .S(S), .Y(Y2));
  MUX_2_X_1_main main_9 (.E_1(A1), .E_2(B1), .S(S), .Y(Y1));
  MUX_2_X_1_main main_10 (.E_1(A0), .E_2(B0), .S(S), .Y(Y0));
endmodule
