// Logisim project MUX 2 X 1.circ as structural Verilog: 1 circuit, main circuit main
// MUX
module main (
  input  S,
  input  E_1,
  input  E_2,
  output Y
);

  wire _1_out, _2_out, _3_out;

  not _1 (_1_out, S);
  and _3 (_3_out, _1_out, E_1);
  and _2 (_2_out, S, E_2);
  or _4 (Y, _3_out, _2_out);
endmodule
