// Logisim project MUX 3 X 1.circ as structural Verilog: 1 circuit, main circuit main
// MUX
module main (
  input  S_1,
  input  S_0,
  input  E_1,
  input  E_2,
  input  E_3,
  output Y
);

  wire _1_out, _2_out, _3_out, _4_out, _5_out;

  not _2 (_2_out, S_0);
  not _1 (_1_out, S_1);
  and _3 (_3_out, S_0, _1_out, E_1);
  and _4 (_4_out, _2_out, S_1, E_2);
  and _5 (_5_out, S_0, S_1, E_3);
  or _6 (Y, _3_out, _4_out, _5_out);

  // Notes on the sheet:
  //   ENTRADAS
  //   CONTROLE
  //   SAÍDA
endmodule
