// Logisim project MUX 4 X 1 10 BITS.circ as structural Verilog: 1 circuit, main circuit main
// MUX 4 X 1 10 BITS
module main (
  input  D9,
  input  D8,
  input  D7,
  input  D6,
  input  D5,
  input  D4,
  input  D3,
  input  D2,
  input  D1,
  input  D0,
  input  C9,
  input  C8,
  input  C7,
  input  C6,
  input  C5,
  input  C4,
  input  C3,
  input  C2,
  input  C1,
  input  C0,
  input  B9,
  input  B8,
  input  B7,
  input  B6,
  input  B5,
  input  B4,
  input  B3,
  input  B2,
  input  B1,
  input  B0,
  input  A9,
  input  A8,
  input  A7,
  input  A6,
  input  A5,
  input  A4,
  input  A3,
  input  A2,
  input  A1,
  input  A0,
  input  S1,
  input  S0,
  output Y9,
  output Y8,
  output Y7,
  output Y6,
  output Y5,
  output Y4,
  output Y3,
  output Y2,
  output Y1,
  output Y0
);

  MUX_4_X_1_main main_1 (.E_1(A9), .E_2(B9), .E_3(C9), .E_4(D9), .S1(S1), .S0(S0), .Y(Y9));
  MUX_4_X_1_main main_2 (.E_1(A8), .E_2(B8), .E_3(C8), .E_4(D8), .S1(S1), .S0(S0), .Y(Y8));
  MUX_4_X_1_main main_3 (.E_1(A7), .E_2(B7), .E_3(C7), .E_4(D7), .S1(S1), .S0(S0), .Y(Y7));
  MUX_4_X_1_main main_4 (.E_1(A6), .E_2(B6), .E_3(C6), .E_4(D6), .S1(S1), .S0(S0), .Y(Y6));
  MUX_4_X_1_main main_5 (.E_1(A5), .E_2(B5), .E_3(C5), .E_4(D5), .S1(S1), .S0(S0), .Y(Y5));
  MUX_4_X_1_main main_6 (.E_1(A4), .E_2(B4), .E_3(C4), .E_4(D4), .S1(S1), .S0(S0), .Y(Y4));
  MUX_4_X_1_main main_7 (.E_1(A3), .E_2(B3), .E_3(C3), .E_4(D3), .S1(S1), .S0(S0), .Y(Y3));
  MUX_4_X_1_main main_8 (.E_1(A2), .E_2(B2), .E_3(C2), .E_4(D2), .S1(S1), .S0(S0), .Y(Y2));
  MUX_4_X_1_main main_9 (.E_1(A1), .E_2(B1), .E_3(C1), .E_4(D1), .S1(S1), .S0(S0), .Y(Y1));
  MUX_4_X_1_main main_10 (.E_1(A0), .E_2(B0), .E_3(C0), .E_4(D0), .S1(S1), .S0(S0), .Y(Y0));
endmodule
