// Logisim project MUX 4 X 1.circ as structural Verilog: 1 circuit, main circuit main
// MUX 4 X 1
module main (
  input  S1,
  input  S0,
  input  E_1,
  input  E_2,
  input  E_3,
  input  E_4,
  output Y
);

  wire _1_out, _2_out, _3_out, _4_out, _5_out, _6_out;

  not _2 (_2_out, S0);
  not _1 (_1_out, S1);
  and _3 (_3_out, _2_out, _1_out, E_1);
  and _4 (_4_out, S0, _1_out, E_2);
  and _5 (_5_out, _2_out, S1, E_3);
  and _6 (_6_out, S0, S1, E_4);
  or _7 (Y, _3_out, _4_out, _5_out, _6_out);
endmodule
