// Logisim project SST.circ as structural Verilog: 1 circuit, main circuit main
// SST
module main (
  input  Cin,
  input  S,
  input  A,
  input  B,
  output Q,
  output Cout
);

  wire _1_out, _2_out, _4_out, _5_out;

  xor _1 (_1_out, S, B);
  xor _2 (_2_out, A, _1_out);
  and _5 (_5_out, _1_out, A);
  and _4 (_4_out, Cin, _2_out);
  xor _3 (Q, _2_out, Cin);
  or _6 (Cout, _4_out, _5_out);
endmodule
