// Logisim project ULA 10 BITS.circ as structural Verilog: 1 circuit, main circuit main
module main (
  input  B9,
  input  B8,
  input  B7,
  input  B6,
  input  B5,
  input  B4,
  input  B3,
  input  B2,
  input  B1,
  input  B0,
  input  A9,
  input  A8,
  input  A7,
  input  A6,
  input  A5,
  input  A4,
  input  A3,
  input  A2,
  input  A1,
  input  A0,
  input  Cin,
  input  S_0,
  input  S_1,
  input  S_2,
  input  S_3,
  output Q_0,
  output Q_1,
  output Q_2,
  output Q_3,
  output Q_4,
  output Q_5,
  output Q_6,
  output Q_7,
  output Q_8,
  output Q_9,
  output Cout,
  output O__F,
  output A___B,
  output A___0,
  output B___0,
  output A___B_2,
  output A___B_3
);

  wire main_2_c_3, main_2_q_0, main_2_q_0_2, main_2_q_1, main_2_q_1_2, main_2_q_2, main_2_q_2_2,
       main_2_q_2_3, main_2_q_3, main_2_q_3_2, main_2_q_3_3, main_3_y_0, main_3_y_1, main_3_y_2, main_3_y_3,
       main_3_y_4, main_3_y_5, main_3_y_6, main_3_y_7, main_3_y_8, main_3_y_9, main_4_y0, main_4_y1,
       main_4_y2, main_4_y3, main_4_y4, main_4_y5, main_4_y6, main_4_y7, main_4_y8, main_4_y9, main_5_nand_0,
       main_5_nand_1, main_5_nand_2, main_5_nand_3, main_5_nand_4, main_5_nand_5, main_5_nand_6,
       main_5_nand_7, main_5_nand_8, main_5_nand_9, main_5_nor_0, main_5_nor_1, main_5_nor_2, main_5_nor_3,
       main_5_nor_4, main_5_nor_5, main_5_nor_6, main_5_nor_7, main_5_nor_8, main_5_nor_9, main_5_xor_0,
       main_5_xor_1, main_5_xor_2, main_5_xor_3, main_5_xor_4, main_5_xor_5, main_5_xor_6, main_5_xor_7,
       main_5_xor_8, main_5_xor_9, main_6_y_0, main_6_y_1, main_6_y_2, main_6_y_3, main_6_y_4, main_6_y_5,
       main_6_y_6, main_6_y_7, main_6_y_8, main_6_y_9, main_7_y0, main_7_y1, main_7_y2, main_7_y3, main_7_y4,
       main_7_y5, main_7_y6, main_7_y7, main_7_y8, main_7_y9;

  COMPARADOR_10_BITS_main main_1 (
    .B_9(B9), .B_8(B8), .B_7(B7), .B_6(B6), .B_5(B5), .B_4(B4), .B_3(B3), .B_2(B2), .B_1(B1), .B_0(B0),
    .A_9(A9), .A_8(A8), .A_7(A7), .A_6(A6), .A_5(A5), .A_4(A4), .A_3(A3), .A_2(A2), .A_1(A1), .A_0(A0),
    .Cout(Cout), .C_2(main_2_c_3), .Q_0(main_2_q_1_2), .Q_1(main_2_q_1), .Q_2(main_2_q_2_3),
    .Q_3(main_2_q_3_3), .Q_4(main_2_q_0_2), .Q_5(main_2_q_0), .Q_6(main_2_q_2_2), .Q_7(main_2_q_3_2),
    .Q_8(main_2_q_2), .Q_9(main_2_q_3), .OVER_FLOW(O__F), .A___B(A___B), .A___0(A___0), .A___B_2(A___B_2),
    .B___0(B___0), .A___B_3(A___B_3));
  \ARITMÉTICA_10_BITS_main  main_2 (
    .B_3(B9), .A_3(A9), .B_2(B8), .A_2(A8), .B_3_2(B7), .A_3_2(A7), .B_2_2(B6), .A_2_2(A6), .B_1(B5),
    .A_1(A5), .B_0(B4), .A_0(A4), .B_3_3(B3), .A_3_3(A3), .B_2_3(B2), .A_2_3(A2), .B_1_2(B1), .A_1_2(A1),
    .B_0_2(B0), .A_0_2(A0), .Cout(Cout), .C_3(main_2_c_3), .Q_3(main_2_q_3), .Q_2(main_2_q_2),
    .Q_3_2(main_2_q_3_2), .Q_2_2(main_2_q_2_2), .Q_0(main_2_q_0), .Q_0_2(main_2_q_0_2), .Q_3_3(main_2_q_3_3),
    .Q_2_3(main_2_q_2_3), .Q_1(main_2_q_1), .Q_1_2(main_2_q_1_2), .Cin(Cin), .S_0(S_0), .S_1(S_1));
  DESLOCAMENTO_10_BITS_main main_3 (
    .S_0(S_0), .S1(S_1), .D_9(A9), .D_8(A8), .D_7(A7), .D_6(A6), .D_5(A5), .D_4(A4), .D_3(A3), .D_2(A2),
    .D_1(A1), .D_0(A0), .Y_9(main_3_y_9), .Y_8(main_3_y_8), .Y_7(main_3_y_7), .Y_6(main_3_y_6),
    .Y_5(main_3_y_5), .Y_4(main_3_y_4), .Y_3(main_3_y_3), .Y_2(main_3_y_2), .Y_1(main_3_y_1), .Y_0(main_3_y_0));
  MUX_2_X_1_10_BITS_main main_4 (
    .B9(main_2_q_3), .B8(main_2_q_2), .B7(main_2_q_3_2), .B6(main_2_q_2_2), .B5(main_2_q_0),
    .B4(main_2_q_0_2), .B3(main_2_q_3_3), .B2(main_2_q_2_3), .B1(main_2_q_1), .B0(main_2_q_1_2),
    .A9(main_3_y_9), .A8(main_3_y_8), .A7(main_3_y_7), .A6(main_3_y_6), .A5(main_3_y_5), .A4(main_3_y_4),
    .A3(main_3_y_3), .A2(main_3_y_2), .A1(main_3_y_1), .A0(main_3_y_0), .Y9(main_4_y9), .Y8(main_4_y8),
    .Y7(main_4_y7), .Y6(main_4_y6), .Y5(main_4_y5), .Y4(main_4_y4), .Y3(main_4_y3), .Y2(main_4_y2),
    .Y1(main_4_y1), .Y0(main_4_y0), .S(S_2));
  BIT_A_BIT_10_BITS_main main_5 (
    .A_0(A0), .A_1(A1), .A_2(A2), .A_3(A3), .A_4(A4), .A_5(A5), .A_6(A6), .A_7(A7), .A_8(A8), .A_9(A9),
    .B_0(B0), .B_1(B1), .B_2(B2), .B_3(B3), .B_4(B4), .B_5(B5), .B_6(B6), .B_7(B7), .B_8(B8), .B_9(B9),
    .NAND_0(main_5_nand_0), .NAND_1(main_5_nand_1), .NAND_2(main_5_nand_2), .NAND_3(main_5_nand_3),
    .NAND_4(main_5_nand_4), .NAND_5(main_5_nand_5), .NAND_6(main_5_nand_6), .NAND_7(main_5_nand_7),
    .NAND_8(main_5_nand_8), .NAND_9(main_5_nand_9), .NOR_0(main_5_nor_0), .NOR_1(main_5_nor_1),
    .NOR_2(main_5_nor_2), .NOR_3(main_5_nor_3), .NOR_4(main_5_nor_4), .NOR_5(main_5_nor_5),
    .NOR_6(main_5_nor_6), .NOR_7(main_5_nor_7), .NOR_8(main_5_nor_8), .NOR_9(main_5_nor_9),
    .XOR_0(main_5_xor_0), .XOR_1(main_5_xor_1), .XOR_2(main_5_xor_2), .XOR_3(main_5_xor_3),
    .XOR_4(main_5_xor_4), .XOR_5(main_5_xor_5), .XOR_6(main_5_xor_6), .XOR_7(main_5_xor_7),
    .XOR_8(main_5_xor_8), .XOR_9(main_5_xor_9));
  XOR_10_BITS_main main_6 (
    .E_0(main_7_y0), .E_1(main_7_y1), .E_2(main_7_y2), .E_3(main_7_y3), .E_4(main_7_y4), .E_5(main_7_y5),
    .E_6(main_7_y6), .E_7(main_7_y7), .E_8(main_7_y8), .E_9(main_7_y9), .S_2(S_2), .Y_0(main_6_y_0),
    .Y_1(main_6_y_1), .Y_2(main_6_y_2), .Y_3(main_6_y_3), .Y_4(main_6_y_4), .Y_5(main_6_y_5),
    .Y_6(main_6_y_6), .Y_7(main_6_y_7), .Y_8(main_6_y_8), .Y_9(main_6_y_9));
  MUX_4_X_1_10_BITS_main main_7 (
    .D9(main_5_xor_9), .D8(main_5_xor_8), .D7(main_5_xor_7), .D6(main_5_xor_6), .D5(main_5_xor_5),
    .D4(main_5_xor_4), .D3(main_5_xor_3), .D2(main_5_xor_2), .D1(main_5_xor_1), .D0(main_5_xor_0),
    .C9(main_5_nor_9), .C8(main_5_nor_8), .C7(main_5_nor_7), .C6(main_5_nor_6), .C5(main_5_nor_5),
    .C4(main_5_nor_4), .C3(main_5_nor_3), .C2(main_5_nor_2), .C1(main_5_nor_1), .C0(main_5_nor_0),
    .B9(main_5_nand_9), .B8(main_5_nand_8), .B7(main_5_nand_7), .B6(main_5_nand_6), .B5(main_5_nand_5),
    .B4(main_5_nand_4), .B3(main_5_nand_3), .B2(main_5_nand_2), .B1(main_5_nand_1), .B0(main_5_nand_0),
    .A9(A9), .A8(A8), .A7(A7), .A6(A6), .A5(A5), .A4(A4), .A3(A3), .A2(A2), .A1(A1), .A0(A0), .Y9(main_7_y9),
    .Y8(main_7_y8), .Y7(main_7_y7), .Y6(main_7_y6), .Y5(main_7_y5), .Y4(main_7_y4), .Y3(main_7_y3),
    .Y2(main_7_y2), .Y1(main_7_y1), .Y0(main_7_y0), .S1(S_1), .S0(S_0));
  MUX_2_X_1_10_BITS_main main_8 (
    .B9(main_4_y9), .B8(main_4_y8), .B7(main_4_y7), .B6(main_4_y6), .B5(main_4_y5), .B4(main_4_y4),
    .B3(main_4_y3), .B2(main_4_y2), .B1(main_4_y1), .B0(main_4_y0), .A9(main_6_y_9), .A8(main_6_y_8),
    .A7(main_6_y_7), .A6(main_6_y_6), .A5(main_6_y_5), .A4(main_6_y_4), .A3(main_6_y_3), .A2(main_6_y_2),
    .A1(main_6_y_1), .A0(main_6_y_0), .Y9(Q_9), .Y8(Q_8), .Y7(Q_7), .Y6(Q_6), .Y5(Q_5), .Y4(Q_4), .Y3(Q_3),
    .Y2(Q_2), .Y1(Q_1), .Y0(Q_0), .S(S_3));
endmodule
