// Logisim project XOR 10 BITS.circ as structural Verilog: 1 circuit, main circuit main
// XOR 10 BITS
module main (
  input  S_2,
  input  E_0,
  input  E_1,
  input  E_2,
  input  E_3,
  input  E_4,
  input  E_5,
  input  E_6,
  input  E_7,
  input  E_8,
  input  E_9,
  output Y_0,
  output Y_1,
  output Y_2,
  output Y_3,
  output Y_4,
  output Y_5,
  output Y_6,
  output Y_7,
  output Y_8,
  output Y_9
);

  xor _1 (Y_0, E_0, S_2);
  xor _2 (Y_1, E_1, S_2);
  xor _3 (Y_2, E_2, S_2);
  xor _4 (Y_3, E_3, S_2);
  xor _5 (Y_4, E_4, S_2);
  xor _6 (Y_5, E_5, S_2);
  xor _7 (Y_6, E_6, S_2);
  xor _8 (Y_7, E_7, S_2);
  xor _9 (Y_8, E_8, S_2);
  xor _10 (Y_9, E_9, S_2);
endmodule
